# Fritzing sketch doorlocking (saved by Fritzing 0.9.3b)
breadboards: 1

parts:
  U1 = NodeMCU V3.0
  U2 = 2-Channel 5v Relay Shield [package=relay-2ch5v10a]
  J1 = Dagu DGServo 9g header (male) [package=THT]

nets:
  N1: U1.GND#6, U1.GND#13, U1.GND#16, U1.GND#33, U2.GND
  N2: U1.D7, U2.IN1
  VIN: U1.Vin, U2.VCC
  N3: U2.K1-In, J1.Vcc
  N4: U2.K1-On, J1.pulse

custom parts:
  NodeMCU V3.0: ESP8266 based NodeMCU
  2-Channel 5v Relay Shield: 2 Channel 5v Relay Shield w. 2x SPD-06VDC-SD-C
